# Fritzing sketch led_matrix (saved by Fritzing 0.9.10b)
breadboards: 1

parts:
  Mod1 = Raspberry Pi Pico W
  8x8_LED_Modul_mit_MAX1 = 8x8 LED Modul mit MAX7219 [package=THT]

nets:
  N1: Mod1.pin_3, Mod1.pin_8, Mod1.pin_13, Mod1.pin_18, Mod1.pin_23, Mod1.pin_28, Mod1.pin_33, Mod1.pin_38, 8x8_LED_Modul_mit_MAX1.GND_Eingang
  N2: Mod1.pin_4, 8x8_LED_Modul_mit_MAX1.CLK_Eingang
  N3: Mod1.pin_5, 8x8_LED_Modul_mit_MAX1.DIN_Eingang
  N4: Mod1.pin_7, 8x8_LED_Modul_mit_MAX1.CS_Eingang
  N5: Mod1.pin_40, 8x8_LED_Modul_mit_MAX1.VCC_Eingang

custom parts:
  Raspberry Pi Pico W: Raspberry Pi Pico W. Based around the RP2040 microcontroller the Pico W is a low cost microcontroller device bringing Raspberry Pi quality, cost, and easy of use to the microcontroller space. The areas marked KEEPOUT in pcb silkscreen should not have traces running through them to avoid shorts on a soldered in module!
