# Fritzing sketch oled (saved by Fritzing 0.9.10b)
breadboards: 1

parts:
  OLED1 = OLED 128x64 I2C Monochrome Display
  Mod1 = Raspberry Pi Pico W

nets:
  N1: OLED1.GND, Mod1.pin_3, Mod1.pin_8, Mod1.pin_13, Mod1.pin_18, Mod1.pin_23, Mod1.pin_28, Mod1.pin_33, Mod1.pin_38, Mod1.pin_42
  N2: OLED1.VDD, Mod1.pin_36
  N3: OLED1.SCK, Mod1.pin_2
  N4: OLED1.SDA, Mod1.pin_1

custom parts:
  Raspberry Pi Pico W: Raspberry Pi Pico W. Based around the RP2040 microcontroller the Pico W is a low cost microcontroller device bringing Raspberry Pi quality, cost, and easy of use to the microcontroller space. The areas marked KEEPOUT in pcb silkscreen should not have traces running through them to avoid shorts on a soldered in module!
