# Fritzing sketch oled_tmp36 (saved by Fritzing 0.9.10b)
breadboards: 1

parts:
  OLED1 = OLED 128x64 I2C Monochrome Display
  Mod1 = Raspberry Pi Pico W
  T1 = TMP36 Temperature Sensor [package="TO92 [THT]"]

nets:
  GND: OLED1.GND, Mod1.pin_3, Mod1.pin_8, Mod1.pin_13, Mod1.pin_18, Mod1.pin_23, Mod1.pin_28, Mod1.pin_33, Mod1.pin_38, Mod1.pin_42, T1.GND
  N1: OLED1.VDD, Mod1.pin_36, T1.+Vs
  N2: OLED1.SCK, Mod1.pin_2
  N3: OLED1.SDA, Mod1.pin_1
  N4: Mod1.pin_34, T1.Vout

custom parts:
  Raspberry Pi Pico W: Raspberry Pi Pico W. Based around the RP2040 microcontroller the Pico W is a low cost microcontroller device bringing Raspberry Pi quality, cost, and easy of use to the microcontroller space. The areas marked KEEPOUT in pcb silkscreen should not have traces running through them to avoid shorts on a soldered in module!
